// Logisim project Shmerlard8.circ as structural Verilog: 8 circuits, main circuit main
module main (
  input  [15:0] in_1,
  input  RST,
  input  MAN,
  input  IR_RD,
  input  IR_WR,
  input  RF_RD,
  input  RF_WR,
  input  src_DST,
  input  Yin,
  input  Yout,
  input  [2:0] in_11,
  input  [2:0] in_12,
  output [4:0] OPCODE,
  output [1:0] IR_ADD_DST,
  output [1:0] IR_ADD_SRC
);

  wire CLK;
  wire [2:0] instruction_register_1_reg_sel_dst, instruction_register_1_reg_sel_src;
  wire [15:0] instruction_register_1_d_bus_out, Y_q;

  Clock u_CLK (.out(CLK));
  // Probe on instruction_register_1_reg_sel_src
  // Probe on instruction_register_1_reg_sel_dst
  Register #(.width(16)) Y (.D(instruction_register_1_d_bus_out), .en(Yin), .clk(CLK), .Q(Y_q));  // open: clr
  instruction_register instruction_register_1 (
    .CLK(CLK), .IR_OUT(IR_RD), .D_BUS(instruction_register_1_d_bus_out), .IR_WR_EN(IR_WR), .RST(RST),
    .REG_SEL_DST(instruction_register_1_reg_sel_dst), .Add_DST(IR_ADD_DST), .Add_SRC(IR_ADD_SRC),
    .REG_SEL_SRC(instruction_register_1_reg_sel_src), .OP_CODE(OPCODE),
    .D_BUS_OUT(instruction_register_1_d_bus_out));
  register_file register_file_1 (
    .src_DST(src_DST), .REG_WR(RF_WR), .REG_RD(RF_RD), .CLK(CLK), .RST(RST),
    .REG_SEL_SRC(instruction_register_1_reg_sel_src), .REG_SEL_DST(instruction_register_1_reg_sel_dst),
    .DATA_IN(instruction_register_1_d_bus_out), .DATA_OUT(instruction_register_1_d_bus_out));
  assign instruction_register_1_d_bus_out = MAN ? in_1 : 16'bz;  // Controlled_Buffer controlled_buffer_1
  assign instruction_register_1_d_bus_out = Yout ? Y_q : 16'bz;  // Controlled_Buffer controlled_buffer_2
  // Probe on instruction_register_1_d_bus_out

  // Other names for the same wires on the sheet: REG_SEL_DST[2:0] = in_12; REG_SEL_SRC[2:0] = in_11
endmodule

module register_file (
  input  CLK,
  input  RST,
  input  [15:0] DATA_IN,
  input  REG_WR,
  input  [2:0] REG_SEL_SRC,
  input  [2:0] REG_SEL_DST,
  input  src_DST,
  input  REG_RD,
  output [15:0] DATA_OUT
);

  wire not_1_out, RD_EN_C, RD_EN_D, RD_EN_E, RD_EN_F, RD_EN_REG2, RD_EN_REG3, RD_EN_SP, RD_EN_SR, WR_EN_C,
       WR_EN_D, WR_EN_E, WR_EN_F, WR_EN_REG2, WR_EN_REG3, WR_EN_SP, WR_EN_SR;
  wire [2:0] multiplexer_1_out;
  wire [15:0] C_REG_q, D_REG_q, E_REG_q, F_REG_q, REG2_q, REG3_q, SP_REG_q, STATUS_REG_q;

  Hex_Digit_Display hex_digit_display_1 (.value({1'b0, REG_SEL_SRC}));  // open: dp
  Hex_Digit_Display hex_digit_display_2 (.value({1'b0, REG_SEL_DST}));  // open: dp
  LED led_1 (.in(not_1_out));
  not not_1 (not_1_out, src_DST);
  LED led_2 (.in(src_DST));
  Multiplexer #(.width(3)) multiplexer_1 (.in0(REG_SEL_SRC), .in1(REG_SEL_DST), .out(multiplexer_1_out), .sel(src_DST));
  // Probe on multiplexer_1_out
  Decoder #(.select(3)) decoder_1 (
    .out0(WR_EN_SP), .out1(WR_EN_SR), .out2(WR_EN_REG2), .out3(WR_EN_REG3), .out4(WR_EN_C), .out5(WR_EN_D),
    .out6(WR_EN_E), .out7(WR_EN_F), .sel(multiplexer_1_out), .en(REG_WR));
  Decoder #(.select(3)) decoder_2 (
    .out0(RD_EN_SP), .out1(RD_EN_SR), .out2(RD_EN_REG2), .out3(RD_EN_REG3), .out4(RD_EN_C), .out5(RD_EN_D),
    .out6(RD_EN_E), .out7(RD_EN_F), .sel(multiplexer_1_out), .en(REG_RD));
  Register #(.width(16)) SP_REG (.D(DATA_IN), .en(WR_EN_SP), .clk(CLK), .Q(SP_REG_q), .clr(RST));
  Register #(.width(16)) STATUS_REG (.D(DATA_IN), .en(WR_EN_SR), .clk(CLK), .Q(STATUS_REG_q), .clr(RST));
  Register #(.width(16)) REG2 (.D(DATA_IN), .en(WR_EN_REG2), .clk(CLK), .Q(REG2_q), .clr(RST));
  Register #(.width(16)) REG3 (.D(DATA_IN), .en(WR_EN_REG3), .clk(CLK), .Q(REG3_q), .clr(RST));
  Register #(.width(16)) C_REG (.D(DATA_IN), .en(WR_EN_C), .clk(CLK), .Q(C_REG_q), .clr(RST));
  Register #(.width(16)) D_REG (.D(DATA_IN), .en(WR_EN_D), .clk(CLK), .Q(D_REG_q), .clr(RST));
  Register #(.width(16)) E_REG (.D(DATA_IN), .en(WR_EN_E), .clk(CLK), .Q(E_REG_q), .clr(RST));
  Register #(.width(16)) F_REG (.D(DATA_IN), .en(WR_EN_F), .clk(CLK), .Q(F_REG_q), .clr(RST));
  assign DATA_OUT = RD_EN_SP ? SP_REG_q : 16'bz;  // Controlled_Buffer controlled_buffer_1
  assign DATA_OUT = RD_EN_SR ? STATUS_REG_q : 16'bz;  // Controlled_Buffer controlled_buffer_2
  assign DATA_OUT = RD_EN_REG2 ? REG2_q : 16'bz;  // Controlled_Buffer controlled_buffer_3
  assign DATA_OUT = RD_EN_REG3 ? REG3_q : 16'bz;  // Controlled_Buffer controlled_buffer_4
  assign DATA_OUT = RD_EN_C ? C_REG_q : 16'bz;  // Controlled_Buffer controlled_buffer_5
  assign DATA_OUT = RD_EN_D ? D_REG_q : 16'bz;  // Controlled_Buffer controlled_buffer_6
  assign DATA_OUT = RD_EN_E ? E_REG_q : 16'bz;  // Controlled_Buffer controlled_buffer_7
  assign DATA_OUT = RD_EN_F ? F_REG_q : 16'bz;  // Controlled_Buffer controlled_buffer_8
endmodule

module instruction_register (
  input  CLK,
  input  RST,
  input  IR_OUT,
  input  [15:0] D_BUS,
  input  IR_WR_EN,
  output [15:0] D_BUS_OUT,
  output [2:0] REG_SEL_DST,
  output [1:0] Add_DST,
  output [1:0] Add_SRC,
  output [2:0] REG_SEL_SRC,
  output [4:0] OP_CODE
);

  wire [3:3] IR_q;

  Register #(.width(16)) IR (
    .D(D_BUS), .en(IR_WR_EN), .clk(CLK), .Q({OP_CODE, REG_SEL_SRC, Add_SRC, Add_DST, IR_q[3], REG_SEL_DST}),
    .clr(RST));
  assign D_BUS_OUT = IR_OUT ? {OP_CODE, REG_SEL_SRC, Add_SRC, Add_DST, IR_q[3], REG_SEL_DST} : 16'bz;  // Controlled_Buffer controlled_buffer_1

  // Other names for the same wires on the sheet: IR_L_O = IR_OUT
endmodule

module timing_control (
  input  TC_RST,
  input  CLK,
  output [4:0] T_OUT
);

  Counter #(.max('h1f), .width(5)) counter_1 (
    .clr(TC_RST), .load(1'b0), .up(1'b1), .count(1'b1), .clk(CLK), .Q(T_OUT));  // open: D, carry
endmodule

module memory_registers (
  input  CLK,
  input  RST,
  input  [15:0] D_BUS,
  input  MAR_WR_EN,
  input  [15:0] MEM_DATA_IN,
  input  MDR_WR_EN,
  input  MEM_sel,
  input  WR_sel,
  input  MDR_OUT_EN,
  output [15:0] MEM_ADDRESS_OUT,
  output [15:0] D_BUS_OUT,
  output [15:0] MEM_DATA_OUT,
  output RAM_WR_EN
);

  wire and_1_out, and_2_out, and_3_out, not_1_out, not_2_out;
  wire [15:0] controlled_buffer_1_out, MDR_q;

  assign controlled_buffer_1_out = not_1_out ? D_BUS : 16'bz;  // Controlled_Buffer controlled_buffer_1
  Register #(.width(16)) MAR (.D(D_BUS), .en(MAR_WR_EN), .clk(CLK), .Q(MEM_ADDRESS_OUT), .clr(RST));
  not not_1 (not_1_out, MEM_sel);
  assign controlled_buffer_1_out = and_1_out ? MEM_DATA_IN : 16'bz;  // Controlled_Buffer controlled_buffer_2
  Register #(.width(16)) MDR (.D(controlled_buffer_1_out), .en(MDR_WR_EN), .clk(CLK), .Q(MDR_q), .clr(RST));
  not not_2 (not_2_out, WR_sel);
  and and_1 (and_1_out, MEM_sel, not_2_out);
  assign MEM_DATA_OUT = and_2_out ? MDR_q : 16'bz;  // Controlled_Buffer controlled_buffer_3
  and and_2 (and_2_out, WR_sel, MDR_OUT_EN);
  and and_3 (and_3_out, not_1_out, MDR_OUT_EN);
  assign D_BUS_OUT = and_3_out ? MDR_q : 16'bz;  // Controlled_Buffer controlled_buffer_4

  assign RAM_WR_EN = WR_sel;
endmodule

module program_counter (
  input  CLK,
  input  RST,
  input  PC_OUT_EN,
  input  PC_WR_EN,
  input  PC_INC_EN,
  input  [15:0] D_BUS,
  output [15:0] D_BUS_OUT
);

  wire [15:0] counter_1_q;

  Counter #(.max('hffff), .width(16)) counter_1 (
    .clr(RST), .load(PC_WR_EN), .up(1'b1), .count(PC_INC_EN), .clk(CLK), .D(D_BUS), .Q(counter_1_q));  // open: carry
  assign D_BUS_OUT = PC_OUT_EN ? counter_1_q : 16'bz;  // Controlled_Buffer controlled_buffer_1
endmodule

module alu (
  input  CLK,
  input  RST,
  input  [15:0] D_BUS,
  input  X_IN,
  input  [2:0] ALU_MUX,
  input  [3:0] FL_IN_ONZC,
  input  Y_IN,
  input  Y_OUT,
  output [3:0] FL_OUT,
  output [15:0] D_BUS_OUT
);

  wire [15:0] multiplexer_1_out, X1, Y_ADD, Y_AND, Y_EQ_B, Y_OR, Y_REG_q, Y_SHRA, Y_SHRC, Y_SUB, Y_XOR;

  Register #(.width(16)) X_REG (.D(D_BUS), .en(X_IN), .clk(CLK), .Q(X1), .clr(RST));
  // Probe on Y_AND
  assign Y_AND = D_BUS & X1;  // AND_Gate and_1, 16 bits wide
  // Probe on Y_XOR
  assign Y_XOR = D_BUS ^ X1;  // XOR_Gate xor_1, 16 bits wide
  // Probe on Y_OR
  assign Y_OR = D_BUS | X1;  // OR_Gate or_1, 16 bits wide
  // Probe on Y_ADD
  Adder #(.width(16)) adder_1 (.a(D_BUS), .b(X1), .out(Y_ADD));  // open: cin, cout
  // Probe on Y_SUB
  Subtractor #(.width(16)) subtractor_1 (.a(D_BUS), .b(X1), .out(Y_SUB));  // open: bin, bout
  Multiplexer #(.select(3), .width(16)) multiplexer_1 (
    .in0(Y_SHRA), .in1(Y_SHRA), .in2(Y_ADD), .in3(Y_SUB), .in4(Y_AND), .in5(Y_OR), .in6(Y_XOR), .in7(Y_EQ_B),
    .out(multiplexer_1_out), .sel(ALU_MUX));
  // Probe on Y_SHRA
  Shifter #(.shift("lr"), .width(16)) shifter_1 (.in(D_BUS), .\dist (4'b0001), .out(Y_SHRA));
  // Probe on Y_SHRC
  Shifter #(.shift("rr"), .width(16)) shifter_2 (.in(D_BUS), .\dist (4'b0001), .out(Y_SHRC));
  assign D_BUS_OUT = Y_OUT ? Y_REG_q : 16'bz;  // Controlled_Buffer controlled_buffer_1
  Register #(.width(16)) Y_REG (.D(multiplexer_1_out), .en(Y_IN), .clk(CLK), .Q(Y_REG_q), .clr(RST));

  // Other names for the same wires on the sheet: X2[15:0] = D_BUS
endmodule

module shift_control (
  input  CLK,
  input  RST,
  input  IR_OUT,
  input  SHC_IN,
  input  SHC_DEC,
  input  [15:0] in_6,
  output SHC_EQ0
);

  wire [3:0] counter_1_q;

  // Probe on in_6[3:0]
  Counter #(.max('hf), .width(4)) counter_1 (
    .clr(RST), .load(SHC_IN), .up(1'b0), .count(SHC_DEC), .clk(CLK), .D(in_6[3:0]), .Q(counter_1_q));  // open: carry
  nor nor_1 (SHC_EQ0, counter_1_q[3], counter_1_q[2], counter_1_q[1], counter_1_q[0]);

  // Other names for the same wires on the sheet: IR_L_O = IR_OUT
endmodule
